// Logisim project Cache0.circ as structural Verilog: 1 circuit, main circuit main
module main (
  input  [3:0] Address
);

  wire Clock_out;
  wire [3:0] ram_1_data, ram_2_data;

  // Probe on Address[3:2]
  // Probe on Address[1:0]
  Clock Clock (.out(Clock_out));
  // Probe on ram_1_data
  RAM #(.addrWidth(2), .dataWidth(4)) ram_1 (
    .addr(Address[3:2]), .data(ram_1_data), .clk(Clock_out));  // open: sel, ld, clr
  RAM #(.addrWidth(4), .dataWidth(4)) ram_2 (.addr(Address), .data(ram_2_data), .clk(Clock_out));  // open: sel, ld, clr
  // Probe on ram_2_data
endmodule
