// Logisim project CacheModules.circ as structural Verilog: 1 circuit, main circuit main
module main (
  input  [15:0] in_1
);

  wire and_1_out, CLK, comparator_1_eq, HIT, multiplexer_1_out, VALID_BIT;
  wire [6:0] CACHE_TAG;
  wire [7:0] CACHE_DATA, RAM_DATA;
  wire [15:0] ram_1_data, random_1_out, RND;

  // Probe on {VALID_BIT, CACHE_TAG, CACHE_DATA}
  // Probe on ram_1_data
  RAM #(.dataWidth(16)) ram_1 (.addr(in_1[8:1]), .data(ram_1_data), .clk(CLK), .ld(HIT));  // open: sel, clr
  // Probe on HIT
  Transistor #(.\type ("n"), .width(16)) transistor_1 (
    .in(ram_1_data), .out({VALID_BIT, CACHE_TAG, CACHE_DATA}), .gate(HIT));
  Transistor #(.width(16)) transistor_2 (.in({1'b1, in_1[15:9], RAM_DATA}), .out(ram_1_data), .gate(HIT));
  // Probe on ram_1_data
  // Probe on {1'b1, in_1[15:9], RAM_DATA}
  Comparator #(.width(7)) comparator_1 (.a(in_1[15:9]), .b(CACHE_TAG), .eq(comparator_1_eq));  // open: gt, lt
  and and_1 (and_1_out, comparator_1_eq, VALID_BIT);
  // Probe on and_1_out
  // Probe on VALID_BIT
  Multiplexer #(.enable("false")) multiplexer_1 (.in0(1'b1), .in1(and_1_out), .out(multiplexer_1_out), .sel(HIT));
  Random #(.width(16)) random_1 (.clk(CLK), .out(random_1_out));  // open: next, clr
  D_Flip_Flop d_ff_1 (.clk(CLK), .D(multiplexer_1_out), .Q(HIT), .en(1'b1));  // open: Qn, preset, reset
  RAM #(.addrWidth(16)) ram_2 (.addr(in_1), .data(RAM_DATA), .clk(CLK));  // open: sel, ld, clr
  Register #(.width(16)) register_1 (.D(random_1_out), .en(HIT), .Q(RND), .clk(CLK));  // open: clr
  Clock clock_1 (.out(CLK));
  // Probe on RAM_DATA
  // Probe on RAM_DATA

  // Other names for the same wires on the sheet: ADDRESS[15:0] = in_1; TAG[6:0] = in_1[15:9]; OFFSET = in_1[0];
  //   INDEX[7:0] = in_1[8:1]

  // Notes on the sheet:
  //   MEMORY ADDRESS
  //   CACHE MEMORY
  //   COMPARATOR
  //   CACHE OUT / LOAD
  //   CACHE IN / STORE
  //   RAM
  //   RANDOM ADDRESS GENERATOR
  //   CLOCK
endmodule
