// Logisim project cache01.circ as structural Verilog: 1 circuit, main circuit main
module main (
  input  in_1,
  input  in_2,
  input  in_3,
  output [3:0] out_4,
  output [3:0] out_5,
  output [3:0] out_6,
  output out_7,
  output [1:0] out_8,
  output [3:0] out_9
);

  wire clock_1_out, comparator_1_eq, not_1_out;
  wire [1:0] controlled_buffer_1_out;

  LED MP (.in(comparator_1_eq));
  not not_1 (not_1_out, comparator_1_eq);
  LED MC (.in(not_1_out));
  Counter #(.width(2), .max('h3)) counter_1 (.Q(out_8));  // open: load, D, count, carry, clk, clr
  Clock clock_1 (.out(clock_1_out));
  RAM #(.addrWidth(2), .dataWidth(4)) ram_1 (
    .addr(out_8), .data(out_6), .sel(out_7), .clk(clock_1_out), .ld(in_2), .clr(in_3));
  Comparator #(.width(4)) comparator_1 (.a(out_6), .b(out_9), .eq(comparator_1_eq));  // open: gt, lt
  Multiplexer #(.width(4)) multiplexer_1 (.in0(out_6), .in1(out_5), .out(out_4), .sel(comparator_1_eq));  // open: en
  assign controlled_buffer_1_out = comparator_1_eq ? out_8 : 2'bz;  // Controlled_Buffer controlled_buffer_1
  RAM #(.addrWidth(4), .dataWidth(4)) ram_2 (
    .addr({{2{in_1}}, controlled_buffer_1_out}), .data(out_5), .sel(comparator_1_eq), .clk(clock_1_out),
    .ld(comparator_1_eq));  // open: clr
endmodule
