// Logisim project rascunho_cache.circ as structural Verilog: 1 circuit, main circuit main
module main (
  input  [2:0] WRITE_TAG,
  input  [2:0] WRITE_INDEX,
  input  [7:0] WRITE_DATA,
  input  WRITE_BIT_VALID,
  input  [8:0] MEMORY_ADDRESS,
  output [7:0] DADOS,
  output HIT_OR_MISS
);

  wire CLK, comparator_1_eq, demultiplexer_2_out0, demultiplexer_2_out1, demultiplexer_2_out2,
       demultiplexer_2_out3, demultiplexer_2_out4, demultiplexer_2_out5, demultiplexer_2_out6,
       demultiplexer_2_out7, multiplexer_2_out, register_8_q, register_10_q, register_11_q, register_12_q,
       register_13_q, register_14_q, register_15_q, register_16_q;
  wire [2:0] demultiplexer_1_out0, demultiplexer_1_out1, demultiplexer_1_out2, demultiplexer_1_out3,
       demultiplexer_1_out4, demultiplexer_1_out5, demultiplexer_1_out6, demultiplexer_1_out7,
       multiplexer_1_out, register_1_q, register_2_q, register_3_q, register_4_q, register_5_q, register_6_q,
       register_7_q, register_9_q;
  wire [7:0] demultiplexer_3_out0, demultiplexer_3_out1, demultiplexer_3_out2, demultiplexer_3_out3,
       demultiplexer_3_out4, demultiplexer_3_out5, demultiplexer_3_out6, demultiplexer_3_out7, register_17_q,
       register_18_q, register_19_q, register_20_q, register_21_q, register_22_q, register_23_q,
       register_24_q;

  Register #(.width(3)) register_1 (.D(demultiplexer_1_out0), .Q(register_1_q), .clk(CLK));  // open: en, clr
  Register #(.width(3)) register_2 (.D(demultiplexer_1_out1), .Q(register_2_q), .clk(CLK));  // open: en, clr
  Register #(.width(3)) register_3 (.D(demultiplexer_1_out2), .Q(register_3_q), .clk(CLK));  // open: en, clr
  Clock clock_1 (.out(CLK));
  Demultiplexer #(.select(3), .width(3), .enable("false")) demultiplexer_1 (
    .out0(demultiplexer_1_out0), .out1(demultiplexer_1_out1), .out2(demultiplexer_1_out2),
    .out3(demultiplexer_1_out3), .out4(demultiplexer_1_out4), .out5(demultiplexer_1_out5),
    .out6(demultiplexer_1_out6), .out7(demultiplexer_1_out7), .in(WRITE_TAG), .sel(WRITE_INDEX));
  Register #(.width(3)) register_4 (.D(demultiplexer_1_out4), .Q(register_4_q), .clk(CLK));  // open: en, clr
  Register #(.width(3)) register_5 (.D(demultiplexer_1_out3), .Q(register_5_q), .clk(CLK));  // open: en, clr
  Multiplexer #(.select(3), .width(3), .enable("false")) multiplexer_1 (
    .in0(register_1_q), .in1(register_2_q), .in2(register_3_q), .in3(register_5_q), .in4(register_4_q),
    .in5(register_6_q), .in6(register_7_q), .in7(register_9_q), .out(multiplexer_1_out),
    .sel(MEMORY_ADDRESS[5:3]));
  Comparator #(.width(3)) comparator_1 (
    .a(multiplexer_1_out), .b(MEMORY_ADDRESS[8:6]), .eq(comparator_1_eq));  // open: gt, lt
  Register #(.width(3)) register_6 (.D(demultiplexer_1_out5), .Q(register_6_q), .clk(CLK));  // open: en, clr
  Register #(.width(3)) register_7 (.D(demultiplexer_1_out6), .Q(register_7_q), .clk(CLK));  // open: en, clr
  Register #(.width(1)) register_8 (.D(demultiplexer_2_out0), .Q(register_8_q), .clk(CLK));  // open: en, clr
  Register #(.width(3)) register_9 (.D(demultiplexer_1_out7), .Q(register_9_q), .clk(CLK));  // open: en, clr
  and and_1 (HIT_OR_MISS, comparator_1_eq, multiplexer_2_out);
  Register #(.width(1)) register_10 (.D(demultiplexer_2_out1), .Q(register_10_q), .clk(CLK));  // open: en, clr
  Register #(.width(1)) register_11 (.D(demultiplexer_2_out2), .Q(register_11_q), .clk(CLK));  // open: en, clr
  Demultiplexer #(.select(3), .enable("false")) demultiplexer_2 (
    .out0(demultiplexer_2_out0), .out1(demultiplexer_2_out1), .out2(demultiplexer_2_out2),
    .out3(demultiplexer_2_out3), .out4(demultiplexer_2_out4), .out5(demultiplexer_2_out5),
    .out6(demultiplexer_2_out6), .out7(demultiplexer_2_out7), .in(WRITE_BIT_VALID), .sel(WRITE_INDEX));
  Register #(.width(1)) register_12 (.D(demultiplexer_2_out4), .Q(register_12_q), .clk(CLK));  // open: en, clr
  Register #(.width(1)) register_13 (.D(demultiplexer_2_out3), .Q(register_13_q), .clk(CLK));  // open: en, clr
  Multiplexer #(.select(3), .enable("false")) multiplexer_2 (
    .in0(register_8_q), .in1(register_10_q), .in2(register_11_q), .in3(register_13_q), .in4(register_12_q),
    .in5(register_14_q), .in6(register_15_q), .in7(register_16_q), .out(multiplexer_2_out),
    .sel(MEMORY_ADDRESS[5:3]));
  Register #(.width(1)) register_14 (.D(demultiplexer_2_out5), .Q(register_14_q), .clk(CLK));  // open: en, clr
  Register #(.width(1)) register_15 (.D(demultiplexer_2_out6), .Q(register_15_q), .clk(CLK));  // open: en, clr
  Register #(.width(1)) register_16 (.D(demultiplexer_2_out7), .Q(register_16_q), .clk(CLK));  // open: en, clr
  Register register_17 (.D(demultiplexer_3_out1), .Q(register_17_q), .clk(CLK));  // open: en, clr
  Register register_18 (.D(demultiplexer_3_out0), .Q(register_18_q), .clk(CLK));  // open: en, clr
  Demultiplexer #(.select(3), .width(8), .enable("false")) demultiplexer_3 (
    .out0(demultiplexer_3_out0), .out1(demultiplexer_3_out1), .out2(demultiplexer_3_out2),
    .out3(demultiplexer_3_out3), .out4(demultiplexer_3_out4), .out5(demultiplexer_3_out5),
    .out6(demultiplexer_3_out6), .out7(demultiplexer_3_out7), .in(WRITE_DATA), .sel(WRITE_INDEX));
  Register register_19 (.D(demultiplexer_3_out3), .Q(register_19_q), .clk(CLK));  // open: en, clr
  Register register_20 (.D(demultiplexer_3_out2), .Q(register_20_q), .clk(CLK));  // open: en, clr
  Multiplexer #(.select(3), .width(8), .enable("false")) multiplexer_3 (
    .in0(register_18_q), .in1(register_17_q), .in2(register_20_q), .in3(register_19_q), .in4(register_21_q),
    .in5(register_22_q), .in6(register_24_q), .in7(register_23_q), .out(DADOS), .sel(MEMORY_ADDRESS[5:3]));
  Register register_21 (.D(demultiplexer_3_out4), .Q(register_21_q), .clk(CLK));  // open: en, clr
  Register register_22 (.D(demultiplexer_3_out5), .Q(register_22_q), .clk(CLK));  // open: en, clr
  Register register_23 (.D(demultiplexer_3_out7), .Q(register_23_q), .clk(CLK));  // open: en, clr
  Register register_24 (.D(demultiplexer_3_out6), .Q(register_24_q), .clk(CLK));  // open: en, clr

  // Other names for the same wires on the sheet: OFFSET[2:0] = MEMORY_ADDRESS[2:0]; INDEX[2:0] = MEMORY_ADDRESS[5:3];
  //   TAG[2:0] = MEMORY_ADDRESS[8:6]

  // Notes on the sheet:
  //   COMPARADOR TAG
  //   BIT VALID
endmodule
