// Logisim project contgray4bits.circ as structural Verilog: 1 circuit, main circuit main
module main (
);

  wire and_1_out, and_2_out, and_3_out, and_4_out, and_5_out, and_6_out, and_7_out, and_8_out, and_9_out,
       and_10_out, clock_1_out, not_1_out, not_2_out, nq0, nq1, nq2, nq3, or_1_out, or_2_out, or_3_out,
       or_4_out, or_5_out, q0, q1, q2, q3, xor_1_out, xor_2_out, xor_3_out;

  xor xor_1 (xor_1_out, q3, q2);
  LED led_1 (.in(q3));
  xor xor_2 (xor_2_out, q3, q2);
  not not_1 (not_1_out, xor_1_out);
  LED led_2 (.in(q1));
  LED led_3 (.in(q2));
  LED led_4 (.in(q0));
  Clock clock_1 (.out(clock_1_out));
  and and_1 (and_1_out, xor_2_out, q1);
  and and_2 (and_2_out, not_1_out, nq1);
  D_Flip_Flop d_ff_1 (.clk(clock_1_out), .D(or_1_out), .Q(q0), .Qn(nq0));  // open: preset, en, reset
  or or_1 (or_1_out, and_1_out, and_2_out);
  not not_2 (not_2_out, xor_3_out);
  xor xor_3 (xor_3_out, q3, q2);
  and and_3 (and_3_out, q0, not_2_out);
  or or_2 (or_2_out, and_3_out, and_4_out);
  and and_4 (and_4_out, q1, nq0);
  D_Flip_Flop d_ff_2 (.clk(clock_1_out), .D(or_2_out), .Q(q1), .Qn(nq1));  // open: preset, en, reset
  and and_5 (and_5_out, q2, or_3_out);
  or or_3 (or_3_out, nq3, nq1, q0);
  and and_6 (and_6_out, q1, nq3, nq0);
  or or_4 (or_4_out, and_5_out, and_6_out);
  D_Flip_Flop d_ff_3 (.clk(clock_1_out), .D(or_4_out), .Q(q2), .Qn(nq2));  // open: preset, en, reset
  and and_7 (and_7_out, q0, q3);
  and and_8 (and_8_out, q3, q1);
  and and_9 (and_9_out, q2, nq1, nq0);
  and and_10 (and_10_out, q2, q3);
  or or_5 (or_5_out, and_7_out, and_8_out, and_9_out, and_10_out);
  D_Flip_Flop d_ff_4 (.clk(clock_1_out), .D(or_5_out), .Q(q3), .Qn(nq3));  // open: preset, en, reset
endmodule
