// Logisim project trab2.circ as structural Verilog: 7 circuits, main circuit main
module \Máquina  (
  input  in_1,
  input  in_2,
  input  in_3,
  input  in_4,
  input  in_5
);

  wire clock_1_out, main_1_im, main_1_le, main_1_ll, main_1_t50, main_1_t100;

  Clock clock_1 (.out(clock_1_out));
  LED led_1 (.in(main_1_t50));
  main main_1 (
    ._50c(in_1), ._100c(in_2), .BE(in_3), .BL(in_4), .BC(in_5), .LL(main_1_ll), .IM(main_1_im),
    .LE(main_1_le), .T100(main_1_t100), .T50(main_1_t50), .in_1(clock_1_out));
  LED led_2 (.in(main_1_le));
  LED led_3 (.in(main_1_t100));
  LED led_4 (.in(main_1_ll));
  LED led_5 (.in(main_1_im));
endmodule

module main (
  input  in_1,
  input  _50c,
  input  _100c,
  input  BE,
  input  BL,
  input  BC,
  output T50,
  output T100,
  output LE,
  output LL,
  output IM
);

  wire _2NQ0, _2Q0, _3NQ0, _3NQ1, _3Q0, _3Q1, _4NQ0, _4NQ1, _4Q0, _4Q1, and_1_out, and_2_out, and_4_out,
       and_5_out, and_7_out, and_8_out, BE1, BE2, BL_t, dinheiro_1_out_7, dinheiro_1_out_8, n50c_1_out_3,
       n100c_1_out_4, n100c_1_out_7, NQ0, NQ1, or_2_out, Q0, Q1;

  and and_1 (and_1_out, _3Q1, _3Q0);
  BE_BL be_bl_1 (.BE(BE), .BL(BL), .out_4(BE1), .out_5(BE2), .out_6(BL_t), .Q1(Q1));
  and and_2 (and_2_out, _4Q0, NQ1, NQ0);
  or or_1 (T50, and_1_out, and_2_out);
  and and_3 (T100, _4Q1, NQ1, NQ0);
  LED led_1 (.in(dinheiro_1_out_7));
  LED led_2 (.in(dinheiro_1_out_8));
  or or_2 (or_2_out, and_4_out, LE, LL);
  and and_4 (and_4_out, in_1, BC);
  and and_5 (and_5_out, _3NQ1, _3Q0);
  or or_3 (LE, and_5_out, _2Q0);
  Dinheiro dinheiro_1 (
    .X0(_50c), .X1(_100c), .in_1(in_1), .out_7(dinheiro_1_out_7), .out_8(dinheiro_1_out_8), .RESET(or_2_out),
    .out_5(Q1), .out_6(Q0), .out_10(NQ0), .out_9(NQ1));
  Cancelar cancelar_1 (.in_1(in_1), .Q0C(Q0), .Q1(Q1), .out_4(_4Q1), .out_5(_4NQ1), .out_6(_4Q0), .out_7(_4NQ0));
  and and_6 (LL, _3Q1, _3NQ0);
  and and_7 (and_7_out, Q1, Q0);
  or or_4 (IM, and_7_out, and_8_out);
  _50C u_50c_1 (.BE(BE1), .CLK(in_1), .out_3(n50c_1_out_3), .out_4(_2Q0), .out_5(_2NQ0));
  LED led_3 (.in(n50c_1_out_3));
  _100C u_100c_1 (
    .BL(BL_t), .BE(BE2), .CLK(in_1), .out_4(n100c_1_out_4), .out_5(_3Q1), .out_6(_3Q0),
    .out_7(n100c_1_out_7), .out_8(_3NQ1), .out_9(_3NQ0));
  LED led_4 (.in(n100c_1_out_7));
  LED led_5 (.in(n100c_1_out_4));
  and and_8 (and_8_out, Q1, NQ0);

  // Other names for the same wires on the sheet: _50 = _50c; _100 = _100c; CLK = in_1
endmodule

module Dinheiro (
  input  in_1,
  input  X0,
  input  X1,
  input  RESET,
  output out_5,
  output out_6,
  output out_7,
  output out_8,
  output out_9,
  output out_10
);

  wire and_1_out, and_2_out, and_3_out, and_4_out, NX0, NX1, or_1_out, or_2_out, or_3_out, or_4_out;

  not not_1 (NX0, X0);
  not not_2 (NX1, X1);
  or or_1 (or_1_out, X1, NX0);
  and and_1 (and_1_out, or_1_out, out_9, out_6);
  and and_2 (and_2_out, NX1, X0, out_10, out_9);
  D_Flip_Flop D0 (.clk(in_1), .D(or_2_out), .Q(out_6), .Qn(out_10), .reset(RESET));  // open: preset, en
  or or_2 (or_2_out, and_1_out, and_2_out);
  and and_3 (and_3_out, X1, NX0);
  or or_3 (or_3_out, and_3_out, and_4_out);
  and and_4 (and_4_out, X0, NX1, out_6);
  D_Flip_Flop D1 (.clk(in_1), .D(or_4_out), .Q(out_5), .Qn(out_9), .reset(RESET));  // open: preset, en
  or or_4 (or_4_out, out_5, or_3_out);

  assign out_7 = out_5;
  assign out_8 = out_6;

  // Other names for the same wires on the sheet: NQ0 = out_10; NQ1 = out_9; Q0 = out_6; Q1 = out_5
endmodule

module BE_BL (
  input  BE,
  input  Q1,
  input  BL,
  output out_4,
  output out_5,
  output out_6
);

  wire demultiplexer_1_out0, demultiplexer_1_out1;

  Demultiplexer demultiplexer_1 (
    .out0(demultiplexer_1_out0), .out1(demultiplexer_1_out1), .in(1'b1), .sel(Q1));  // open: en
  and and_1 (out_4, BE, demultiplexer_1_out0);
  and and_2 (out_5, demultiplexer_1_out1, BE);
  and and_3 (out_6, demultiplexer_1_out1, BL);
endmodule

module _50C (
  input  CLK,
  input  BE,
  output out_3,
  output out_4,
  output out_5
);

  wire and_1_out;

  and and_1 (and_1_out, BE, out_5);
  D_Flip_Flop d_ff_1 (.clk(CLK), .D(and_1_out), .Q(out_3), .Qn(out_5));  // open: preset, en, reset

  assign out_4 = out_3;

  // Other names for the same wires on the sheet: NQ0 = out_5; Q0 = out_3
endmodule

module _100C (
  input  CLK,
  input  BE,
  input  BL,
  output out_4,
  output out_5,
  output out_6,
  output out_7,
  output out_8,
  output out_9
);

  wire and_1_out, and_2_out, and_3_out, and_4_out, NBE, NBL, or_1_out, or_2_out;

  not not_1 (NBE, BE);
  not not_2 (NBL, BL);
  and and_1 (and_1_out, NBL, BE);
  and and_2 (and_2_out, out_8, or_1_out);
  or or_1 (or_1_out, out_6, and_1_out);
  D_Flip_Flop d_ff_1 (.clk(CLK), .D(and_2_out), .Q(out_6), .Qn(out_9));  // open: preset, en, reset
  and and_3 (and_3_out, out_8, out_6);
  or or_2 (or_2_out, and_3_out, and_4_out);
  and and_4 (and_4_out, BL, NBE, out_9);
  D_Flip_Flop d_ff_2 (.clk(CLK), .D(or_2_out), .Q(out_4), .Qn(out_8));  // open: preset, en, reset

  assign out_5 = out_4;
  assign out_7 = out_6;

  // Other names for the same wires on the sheet: NQ0 = out_9; NQ1 = out_8; Q0 = out_6; Q1 = out_4
endmodule

module Cancelar (
  input  in_1,
  input  Q0C,
  input  Q1,
  output out_4,
  output out_5,
  output out_6,
  output out_7
);

  wire BC1, BC2, demultiplexer_1_out0, demultiplexer_1_out1, not_1_out;

  Demultiplexer demultiplexer_1 (
    .out0(demultiplexer_1_out0), .out1(demultiplexer_1_out1), .in(1'b1), .sel(Q1));  // open: en
  and and_1 (BC1, Q0C, demultiplexer_1_out0);
  and and_2 (BC2, demultiplexer_1_out1, not_1_out);
  not not_1 (not_1_out, Q0C);
  D_Flip_Flop _50C (.clk(in_1), .D(BC1), .Q(out_6), .Qn(out_7));  // open: preset, en, reset
  D_Flip_Flop _100C (.clk(in_1), .D(BC2), .Q(out_4), .Qn(out_5));  // open: preset, en, reset

  // Other names for the same wires on the sheet: CLK = in_1; NQ0 = out_7; NQ1 = out_5; Q0 = out_6; Q1_t = out_4
endmodule
