// Logisim project Subtractor.circ as structural Verilog: 5 circuits, main circuit main
module main (
  input  A3,
  input  A2,
  input  A1,
  input  A0,
  input  B3,
  input  B2,
  input  B1,
  input  B0,
  output out_9,
  output out_10,
  output out_11,
  output out_12,
  output out_13
);

  wire meiosomador1bit_1_out_2, meiosomador1bit_1_out_3, not_1_out, not_2_out, not_3_out, not_4_out,
       not_5_out, not_6_out, not_7_out, not_8_out, somador4bits_1_out_11, somador4bits_1_out_12,
       somador4bits_1_out_13, somador4bits_1_out_14, somadorcompleto1bit_1_out_3,
       somadorcompleto1bit_2_out_3, somadorcompleto1bit_2_out_4, somadorcompleto1bit_3_out_3,
       somadorcompleto1bit_3_out_4;

  not not_1 (not_1_out, somador4bits_1_out_11);
  SomadorCompleto1Bit somadorcompleto1bit_1 (
    .A(not_1_out), .VEM(somadorcompleto1bit_2_out_4), .out_3(somadorcompleto1bit_1_out_3));  // open: out_4
  Multiplexer multiplexer_1 (
    .in0(somadorcompleto1bit_1_out_3), .in1(somador4bits_1_out_11), .out(out_10), .sel(out_9));  // open: en
  not not_2 (not_2_out, B3);
  not not_3 (not_3_out, somador4bits_1_out_12);
  SomadorCompleto1Bit somadorcompleto1bit_2 (
    .A(not_3_out), .VEM(somadorcompleto1bit_3_out_4), .out_3(somadorcompleto1bit_2_out_3),
    .out_4(somadorcompleto1bit_2_out_4));
  Multiplexer multiplexer_2 (
    .in0(somadorcompleto1bit_2_out_3), .in1(somador4bits_1_out_12), .out(out_11), .sel(out_9));  // open: en
  not not_4 (not_4_out, B2);
  not not_5 (not_5_out, B1);
  not not_6 (not_6_out, B0);
  Somador4bits somador4bits_1 (
    .out_10(out_9), .in_9(1'b1), .in_2(A3), .in_3(A2), .in_1(A1), .in_4(A0), .in_5(not_2_out),
    .in_6(not_4_out), .in_7(not_5_out), .in_8(not_6_out), .out_11(somador4bits_1_out_11),
    .out_12(somador4bits_1_out_12), .out_13(somador4bits_1_out_13), .out_14(somador4bits_1_out_14));
  not not_7 (not_7_out, somador4bits_1_out_13);
  SomadorCompleto1Bit somadorcompleto1bit_3 (
    .A(not_7_out), .VEM(meiosomador1bit_1_out_3), .out_3(somadorcompleto1bit_3_out_3),
    .out_4(somadorcompleto1bit_3_out_4));
  Multiplexer multiplexer_3 (
    .in0(somadorcompleto1bit_3_out_3), .in1(somador4bits_1_out_13), .out(out_12), .sel(out_9));  // open: en
  not not_8 (not_8_out, somador4bits_1_out_14);
  MeioSomador1Bit meiosomador1bit_1 (.A(not_8_out), .out_2(meiosomador1bit_1_out_2), .out_3(meiosomador1bit_1_out_3));
  Multiplexer multiplexer_4 (
    .in0(meiosomador1bit_1_out_2), .in1(somador4bits_1_out_14), .out(out_13), .sel(out_9));  // open: en
endmodule

module Somador4bits (
  input  in_1,
  input  in_2,
  input  in_3,
  input  in_4,
  input  in_5,
  input  in_6,
  input  in_7,
  input  in_8,
  input  in_9,
  output out_10,
  output out_11,
  output out_12,
  output out_13,
  output out_14
);

  wire somadorcompleto_2_out_5, somadorcompleto_3_out_5, somadorcompleto_4_out_5;

  SomadorCompleto somadorcompleto_1 (.A(in_2), .B(in_5), .VEM(somadorcompleto_2_out_5), .out_4(out_11), .out_5(out_10));
  SomadorCompleto somadorcompleto_2 (
    .A(in_3), .B(in_6), .VEM(somadorcompleto_3_out_5), .out_4(out_12), .out_5(somadorcompleto_2_out_5));
  SomadorCompleto somadorcompleto_3 (
    .A(in_1), .B(in_7), .VEM(somadorcompleto_4_out_5), .out_4(out_13), .out_5(somadorcompleto_3_out_5));
  SomadorCompleto somadorcompleto_4 (.A(in_4), .B(in_8), .VEM(in_9), .out_4(out_14), .out_5(somadorcompleto_4_out_5));
endmodule

module SomadorCompleto (
  input  A,
  input  B,
  input  VEM,
  output out_4,
  output out_5
);

  wire and_1_out, and_2_out, and_3_out, and_4_out, and_5_out, and_6_out, and_7_out, and_8_out, not_1_out,
       not_2_out, not_3_out, not_4_out, not_5_out, not_6_out, not_7_out, not_8_out, not_9_out;

  not not_1 (not_1_out, A);
  not not_2 (not_2_out, VEM);
  not not_3 (not_3_out, B);
  not not_4 (not_4_out, VEM);
  not not_5 (not_5_out, A);
  not not_6 (not_6_out, B);
  not not_7 (not_7_out, VEM);
  not not_8 (not_8_out, A);
  not not_9 (not_9_out, B);
  and and_1 (and_1_out, not_1_out, B, not_2_out);
  and and_2 (and_2_out, A, not_3_out, not_4_out);
  and and_3 (and_3_out, not_5_out, not_6_out, VEM);
  and and_4 (and_4_out, A, B, VEM);
  and and_5 (and_5_out, A, B, not_7_out);
  and and_6 (and_6_out, not_8_out, B, VEM);
  and and_7 (and_7_out, A, not_9_out, VEM);
  and and_8 (and_8_out, A, B, VEM);
  or or_1 (out_4, and_1_out, and_2_out, and_3_out, and_4_out);
  or or_2 (out_5, and_5_out, and_6_out, and_7_out, and_8_out);
endmodule

module MeioSomador1Bit (
  input  A,
  output out_2,
  output out_3
);

  wire not_1_out;

  not not_1 (not_1_out, A);
  and and_1 (out_2, not_1_out, 1'b1);
  and and_2 (out_3, A, 1'b1);
endmodule

module SomadorCompleto1Bit (
  input  A,
  input  VEM,
  output out_3,
  output out_4
);

  wire and_1_out, and_2_out, not_1_out, not_2_out;

  not not_1 (not_1_out, VEM);
  not not_2 (not_2_out, A);
  and and_1 (and_1_out, A, not_1_out);
  and and_2 (and_2_out, VEM, not_2_out);
  or or_1 (out_3, and_1_out, and_2_out);
  and and_3 (out_4, A, VEM);
endmodule
