// Logisim project TrabalhoFinalizado.circ as structural Verilog: 1 circuit, main circuit main
module main (
  input  A,
  input  A_2,
  input  A_3,
  input  A_4,
  input  B,
  input  B_2,
  input  B_3,
  input  B_4
);

  wire main_1_out_9, main_1_out_10, main_1_out_11, main_1_out_12, main_1_out_13, main_2_out_5, main_2_out_6,
       main_2_out_7, main_2_out_8, main_2_out_9, main_2_out_10, main_2_out_11, not_1_out;

  not not_1 (not_1_out, main_1_out_9);
  Subtractor_main main_1 (
    .A3(A), .A2(A_2), .A1(A_3), .A0(A_4), .B3(B), .B2(B_2), .B1(B_3), .B0(B_4), .out_10(main_1_out_10),
    .out_11(main_1_out_11), .out_13(main_1_out_13), .out_12(main_1_out_12), .out_9(main_1_out_9));
  Display_main main_2 (
    .out_5(main_2_out_5), .out_6(main_2_out_6), .out_7(main_2_out_7), .out_8(main_2_out_8),
    .out_9(main_2_out_9), .out_10(main_2_out_10), .out_11(main_2_out_11), .A(main_1_out_10),
    .B(main_1_out_11), .C(main_1_out_12), .D(main_1_out_13));
  _7_Segment_Display u_7_segment_display_1 (
    .g(main_2_out_11), .f(main_2_out_10), .a(main_2_out_5), .b(main_2_out_6), .e(main_2_out_9),
    .d(main_2_out_8), .c(main_2_out_7), .dp(not_1_out));
endmodule
